# Fritzing sketch full_PCB (saved by Fritzing 0.9.3b)
breadboards: 1

parts:
  Part1 = BluePill
  U1 = L9110 H-bridge module [part_number="L9110 H-bridge"]
  U2 = L9110 H-bridge module [part_number="L9110 H-bridge"]
  M1 = Getriebemotor
  M2 = Getriebemotor
  M3 = Getriebemotor
  M4 = Getriebemotor
  Stromversorgung_Beradboard1 = Stromversorgung Beradboard [package=THT]
  hc-sr1 = hc-sr04
  hc-sr2 = hc-sr04
  OLED1 = OLED 128x64 I2C Monochrome Display GND-VDD
  OLED2 = OLED 128x64 I2C Monochrome Display GND-VDD
  SERVO1 = Tower Pro SG90 servo [part_number=101246]
  SERVO2 = Tower Pro SG90 servo [part_number=101246]
  Part2 = Gabellichtschranke
  Part3 = Gabellichtschranke
  U3 = TCRT5000 Line Tracker
  U4 = TCRT5000 Line Tracker

nets:
  N1: Part1.C14, hc-sr1.Echo
  N2: Part1.C15, U4.Do
  N3: Part1.A0, U4.Ao
  N4: Part1.A1, U3.Ao
  N5: Part1.A3, SERVO1.Signal
  N6: Part1.A5, hc-sr2.Trig
  N7: Part1.A6, hc-sr2.Echo
  N8: Part1.A7, U1.B-IA
  N9: Part1.B10, OLED1.SCK
  N10: Part1.B11, OLED1.SDA
  GND: Part1.GND3, U1.GND, U2.GND
  N11: Part1.B7, OLED2.SDA
  N12: Part1.B6, OLED2.SCK
  N13: Part1.B5, U2.B-IA
  N14: Part1.B4, Part3.OUT
  N15: Part1.B3, SERVO2.Signal
  N16: Part1.A15, hc-sr1.Trig
  N17: Part1.A10, U1.B-IB
  N18: Part1.A9, U1.A-IA
  N19: Part1.A8, U2.B-IB
  N20: Part1.B15, U2.A-IA
  N21: Part1.B14, U2.A-IB
  N22: Part1.B13, U1.A-IB
  N23: Part1.B12, Part2.OUT
  N24: Part1.A2, U3.Do
  VCC: U1.VCC, U2.VCC
  N25: U1.MOTOR_A-A, M1.pin_2
  N26: U1.MOTOR_A-B, M1.pin_1
  N27: U1.MOTOR_B-A, M3.pin_2
  N28: U1.MOTOR_B-B, M3.pin_1
  N29: U2.MOTOR_A-A, M2.pin_2
  N30: U2.MOTOR_A-B, M2.pin_1
  N31: U2.MOTOR_B-A, M4.pin_2
  N32: U2.MOTOR_B-B, M4.pin_1
  N33: Stromversorgung_Beradboard1.+5_Volt_1, Stromversorgung_Beradboard1.Ground_1
  N34: Stromversorgung_Beradboard1.+5_Volt_2, Stromversorgung_Beradboard1.Ground_2
  N35: Stromversorgung_Beradboard1.+5_Volt_3, Stromversorgung_Beradboard1.Ground_3
  N36: Stromversorgung_Beradboard1.+3_Volt_1, Stromversorgung_Beradboard1.Ground_4
  N37: Stromversorgung_Beradboard1.+3_Volt_2, Stromversorgung_Beradboard1.Ground_5
  N38: Stromversorgung_Beradboard1.+3_Volt_3, Stromversorgung_Beradboard1.Ground_6

notes:
  GND
  VCC
  interrupt
  digital in
  digital out
  analog in
  analog out/PWM
  I2C SCL
  I2C SDA

custom parts:
  OLED 128x64 I2C Monochrome Display GND-VDD: OLED 128x64 I2C Monochrome Display. Note: there are two variants of this part, this one is the GND VDD SCK SDA variant. The other is VDD GND SCK SDA. Make sure you select the part that matches your module as using the incorrect part will probably destroy your module! In addition the mounting holes are marked on silkscreen but not by default drilled. If you want drilled mounting holes, copy a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
  Tower Pro SG90 servo: Original file by John De Cristofaro http://www.adafruit.com/products/1449 Adafruit Feedback Servo (Small) Edited by: e-radionica.com 28/9/2015
  TCRT5000 Line Tracker: A line tracker module based on TCRT5000 (Vishay)
