# Fritzing sketch full_nano (saved by Fritzing 0.9.3b)
breadboards: 1

parts:
  U1 = L9110 H-bridge module [part_number="L9110 H-bridge"]
  M1 = Getriebemotor
  M3 = Getriebemotor
  Stromversorgung_Beradboard1 = Stromversorgung Beradboard [package=THT]
  hc-sr1 = hc-sr04
  hc-sr2 = hc-sr04
  OLED1 = OLED 128x64 I2C Monochrome Display GND-VDD
  OLED2 = OLED 128x64 I2C Monochrome Display GND-VDD
  SERVO1 = Tower Pro SG90 servo [part_number=101246]
  SERVO2 = Tower Pro SG90 servo [part_number=101246]
  Part2 = Gabellichtschranke
  Part3 = Gabellichtschranke
  U3 = TCRT5000 Line Tracker
  U4 = TCRT5000 Line Tracker
  Part4 = Arduino Nano (Rev3.0)

nets:
  N1: U1.B-IA, Part4.D7
  N2: U1.B-IB, Part4.D6
  GND: U1.GND, Stromversorgung_Beradboard1.Ground_1#15, Part4.GND
  N3: U1.VCC, Stromversorgung_Beradboard1.+5_/_+3_Volt_4#13
  N4: U1.A-IA, Part4.D5
  N5: U1.A-IB, Part4.D4
  N6: U1.MOTOR_A-A, M1.pin_2
  N7: U1.MOTOR_A-B, M1.pin_1
  N8: U1.MOTOR_B-A, M3.pin_2
  N9: U1.MOTOR_B-B, M3.pin_1
  N10: hc-sr1.Trig, Part4.D11/MOSI
  N11: hc-sr1.Echo, Part4.D10
  N12: hc-sr2.Trig, Part4.D9
  N13: hc-sr2.Echo, Part4.D8
  N14: OLED1.SCK, OLED2.SCK, Part4.A5
  N15: OLED1.SDA, OLED2.SDA, Part4.A4
  N16: SERVO1.Signal, Part4.A3
  N17: SERVO2.Signal, Part4.D12/MISO
  N18: Part2.OUT, Part4.D2
  N19: Part3.OUT, Part4.D3
  N20: U3.Do, Part4.A7
  N21: U3.Ao, Part4.A1
  N22: U4.Do, Part4.A6
  N23: U4.Ao, Part4.A0

notes:
  GND
  VCC
  interrupt
  digital in
  digital out
  analog in
  analog out/PWM
  I2C SCL
  I2C SDA

custom parts:
  OLED 128x64 I2C Monochrome Display GND-VDD: OLED 128x64 I2C Monochrome Display. Note: there are two variants of this part, this one is the GND VDD SCK SDA variant. The other is VDD GND SCK SDA. Make sure you select the part that matches your module as using the incorrect part will probably destroy your module! In addition the mounting holes are marked on silkscreen but not by default drilled. If you want drilled mounting holes, copy a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
  Tower Pro SG90 servo: Original file by John De Cristofaro http://www.adafruit.com/products/1449 Adafruit Feedback Servo (Small) Edited by: e-radionica.com 28/9/2015
  TCRT5000 Line Tracker: A line tracker module based on TCRT5000 (Vishay)
