# Fritzing sketch full_uno (saved by Fritzing 0.9.3b)
breadboards: 1

parts:
  U1 = L9110 H-bridge module [part_number="L9110 H-bridge"]
  M1 = Getriebemotor
  M3 = Getriebemotor
  Stromversorgung_Beradboard1 = Stromversorgung Beradboard [package=THT]
  hc-sr1 = hc-sr04
  hc-sr2 = hc-sr04
  OLED1 = OLED 128x64 I2C Monochrome Display GND-VDD
  OLED2 = OLED 128x64 I2C Monochrome Display GND-VDD
  SERVO1 = Tower Pro SG90 servo [part_number=101246]
  SERVO2 = Tower Pro SG90 servo [part_number=101246]
  Part2 = Gabellichtschranke
  Part3 = Gabellichtschranke
  U3 = TCRT5000 Line Tracker
  U4 = TCRT5000 Line Tracker
  Part4 = Arduino Uno (Rev3)

nets:
  N1: U1.B-IA, Part4.D7
  N2: U1.B-IB, Part4.D6_PWM
  N3: U1.A-IA, Part4.D5_PWM
  N4: U1.A-IB, Part4.D4
  N5: U1.MOTOR_A-A, M1.pin_2
  N6: U1.MOTOR_A-B, M1.pin_1
  N7: U1.MOTOR_B-A, M3.pin_2
  N8: U1.MOTOR_B-B, M3.pin_1
  N9: Stromversorgung_Beradboard1.+5_Volt_1, Stromversorgung_Beradboard1.Ground_1#3
  N10: Stromversorgung_Beradboard1.+5_Volt_2, Stromversorgung_Beradboard1.Ground_2
  N11: Stromversorgung_Beradboard1.+5_Volt_3, Stromversorgung_Beradboard1.Ground_3
  N12: Stromversorgung_Beradboard1.+3_Volt_1, Stromversorgung_Beradboard1.Ground_4
  N13: Stromversorgung_Beradboard1.+3_Volt_2, Stromversorgung_Beradboard1.Ground_5
  N14: Stromversorgung_Beradboard1.+3_Volt_3, Stromversorgung_Beradboard1.Ground_6
  N15: hc-sr1.Trig, Part4.D11_PWM/MOSI
  N16: hc-sr1.Echo, Part4.D10_PWM/SS
  N17: hc-sr2.Trig, Part4.D9_PWM
  N18: hc-sr2.Echo, Part4.D8
  N19: OLED1.SCK, OLED2.SCK, Part4.A5/SCL
  N20: OLED1.SDA, OLED2.SDA, Part4.A4/SDA
  N21: SERVO1.Signal, Part4.A3
  N22: SERVO2.Signal, Part4.D12/MISO
  N23: Part2.OUT, Part4.D2
  N24: Part3.OUT, Part4.D3_PWM
  N25: U3.Ao, Part4.A1
  N26: U4.Ao, Part4.A0

notes:
  GND
  VCC
  interrupt
  digital in
  digital out
  analog in
  analog out/PWM
  I2C SCL
  I2C SDA

custom parts:
  OLED 128x64 I2C Monochrome Display GND-VDD: OLED 128x64 I2C Monochrome Display. Note: there are two variants of this part, this one is the GND VDD SCK SDA variant. The other is VDD GND SCK SDA. Make sure you select the part that matches your module as using the incorrect part will probably destroy your module! In addition the mounting holes are marked on silkscreen but not by default drilled. If you want drilled mounting holes, copy a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
  Tower Pro SG90 servo: Original file by John De Cristofaro http://www.adafruit.com/products/1449 Adafruit Feedback Servo (Small) Edited by: e-radionica.com 28/9/2015
  TCRT5000 Line Tracker: A line tracker module based on TCRT5000 (Vishay)
